# Fritzing sketch electric_layout (saved by Fritzing 0.9.3b)
breadboards: 1

parts:
  Raspberry_Pi_1 = Raspberry Pi B rev2
  V1 = DC Power [voltage=5]
  DS1 = DS18B20 1-Wire Temperature Sensor [part_number=DS18B20]
  Ventilator = Small Fan, based on Fan - Ventilador [package=THT]
  D1 = Diode [part_number=IN5822 package=diode-hv]
  R2 = Resistor [tolerance=±5% resistance=1k package="0805 [SMD]"]
  R1 = Resistor [tolerance=±5% resistance=4.7k package="0805 [SMD]"]
  Q2 = Basic FET N-Channel [part_number=IRLZ44N package="D2Pak [SMD]"]
  R4 = Resistor [tolerance=±5% resistance=1k package="0805 [SMD]"]
  R3 = Resistor [tolerance=±5% resistance=1k package="0805 [SMD]"]
  R5 = Resistor [tolerance=±5% resistance=1k package="0805 [SMD]"]
  Teplotny_element = Resistor [tolerance=±5% resistance=220 package="2010 [SMD]"]
  Q1 = Basic FET N-Channel [part_number=IRLZ44N package="D2Pak [SMD]"]
  LED1 = LED - 3mm [color="Red (633nm)" package="3 mm [THT]"]
  R6 = Resistor [tolerance=±5% resistance=100 package="2512 [SMD]"]
  LED2 = smd LED [color="Blue (505nm)" package="0805 [SMD]"]
  R7 = Resistor [tolerance=±5% resistance=100 package="2512 [SMD]"]

nets:
  3V3: Raspberry_Pi_1.3V3, DS1.VDD, R1.Pin_0
  GND: Raspberry_Pi_1.GND, V1.V-, DS1.GND, Q2.source, R3.Pin_1, R5.Pin_1, Q1.source, LED1.cathode, LED2.cathode
  N1: Raspberry_Pi_1.GPIO_23, R4.Pin_0, R7.Pin_0
  N2: Raspberry_Pi_1.GPIO_18, R2.Pin_0, R6.Pin_0
  N3: Raspberry_Pi_1.GPIO_7, DS1.DQ, R1.Pin_1
  N4: V1.V+, Ventilator.5V, D1.C, Teplotny_element.Pin_1
  N5: Ventilator.GND, D1.A, Q2.drain
  N6: R2.Pin_1, R3.Pin_0, Q1.Gate
  N7: Q2.Gate, R4.Pin_1, R5.Pin_0
  N8: Teplotny_element.Pin_0, Q1.drain
  N9: LED1.anode, R6.Pin_1
  N10: LED2.anode, R7.Pin_1

custom parts:
  Small Fan, based on Fan - Ventilador: Small 2-pin fan, commonly used with single-board computers, 3d-printers, etc. This work is based on a much larger fan, as commonly found in desktop computers
